// Logisim project 4bit_mult.circ as structural Verilog: 12 circuits, main circuit main
module main (
  input  in_1,
  input  in_2,
  input  in_3,
  input  in_4,
  input  in_5,
  input  in_6,
  input  in_7,
  input  in_8
);

  wire hex_transcoder_1_out_5, hex_transcoder_1_out_6, hex_transcoder_1_out_7, hex_transcoder_1_out_8,
       hex_transcoder_1_out_9, hex_transcoder_1_out_10, hex_transcoder_1_out_11, hex_transcoder_2_out_5,
       hex_transcoder_2_out_6, hex_transcoder_2_out_7, hex_transcoder_2_out_8, hex_transcoder_2_out_9,
       hex_transcoder_2_out_10, hex_transcoder_2_out_11, n8bit_multiplier_1_out_10,
       n8bit_multiplier_1_out_11, n8bit_multiplier_1_out_12, n8bit_multiplier_1_out_13,
       n8bit_multiplier_1_out_14, n8bit_multiplier_1_out_15, n8bit_multiplier_1_r0, n8bit_multiplier_1_r7;

  _8bit_multiplier u_8bit_multiplier_1 (
    .A3(in_1), .in_2(in_2), .in_3(in_3), .A0(in_4), .B3(in_5), .in_6(in_6), .in_7(in_7), .B0(in_8),
    .R0(n8bit_multiplier_1_r0), .out_10(n8bit_multiplier_1_out_10), .out_11(n8bit_multiplier_1_out_11),
    .out_12(n8bit_multiplier_1_out_12), .out_13(n8bit_multiplier_1_out_13),
    .out_14(n8bit_multiplier_1_out_14), .out_15(n8bit_multiplier_1_out_15), .R7(n8bit_multiplier_1_r7));
  hex_transcoder hex_transcoder_1 (
    .I0(n8bit_multiplier_1_r0), .in_2(n8bit_multiplier_1_out_10), .in_3(n8bit_multiplier_1_out_11),
    .I4(n8bit_multiplier_1_out_12), .out_5(hex_transcoder_1_out_5), .out_6(hex_transcoder_1_out_6),
    .out_7(hex_transcoder_1_out_7), .out_8(hex_transcoder_1_out_8), .out_9(hex_transcoder_1_out_9),
    .out_10(hex_transcoder_1_out_10), .out_11(hex_transcoder_1_out_11));
  hex_transcoder hex_transcoder_2 (
    .I0(n8bit_multiplier_1_out_13), .in_2(n8bit_multiplier_1_out_14), .in_3(n8bit_multiplier_1_out_15),
    .I4(n8bit_multiplier_1_r7), .out_5(hex_transcoder_2_out_5), .out_6(hex_transcoder_2_out_6),
    .out_7(hex_transcoder_2_out_7), .out_8(hex_transcoder_2_out_8), .out_9(hex_transcoder_2_out_9),
    .out_10(hex_transcoder_2_out_10), .out_11(hex_transcoder_2_out_11));
  _7_Segment_Display u_7_segment_display_1 (
    .g(hex_transcoder_2_out_8), .f(hex_transcoder_2_out_9), .a(hex_transcoder_2_out_10),
    .b(hex_transcoder_2_out_11), .e(hex_transcoder_2_out_7), .d(hex_transcoder_2_out_6),
    .c(hex_transcoder_2_out_5), .dp(1'b0));
  _7_Segment_Display u_7_segment_display_2 (
    .g(hex_transcoder_1_out_8), .f(hex_transcoder_1_out_9), .a(hex_transcoder_1_out_10),
    .b(hex_transcoder_1_out_11), .e(hex_transcoder_1_out_7), .d(hex_transcoder_1_out_6),
    .c(hex_transcoder_1_out_5), .dp(1'b0));
endmodule

// FA
module full_adder (
  input  Vi,
  input  A,
  input  B,
  output S,
  output Vi_1
);

  wire and_1_out, and_2_out, and_3_out;

  xor xor_1 (S, Vi, A, B);
  and and_1 (and_1_out, Vi, A);
  and and_2 (and_2_out, Vi, B);
  and and_3 (and_3_out, A, B);
  or or_1 (Vi_1, and_1_out, and_2_out, and_3_out);
endmodule

module _8bit_adder (
  input  A7,
  input  in_2,
  input  in_3,
  input  in_4,
  input  in_5,
  input  in_6,
  input  in_7,
  input  A0,
  input  B7,
  input  in_10,
  input  in_11,
  input  in_12,
  input  in_13,
  input  in_14,
  input  in_15,
  input  B0,
  output R0,
  output out_18,
  output out_19,
  output out_20,
  output out_21,
  output out_22,
  output out_23,
  output R7
);

  wire full_adder_1_vi_1, full_adder_2_vi_1, full_adder_3_vi_1, full_adder_4_vi_1, full_adder_5_vi_1,
       full_adder_6_vi_1, full_adder_7_vi_1, full_adder_8_vi_1;

  full_adder full_adder_1 (.Vi(1'b0), .A(A0), .B(B0), .S(R0), .Vi_1(full_adder_1_vi_1));
  full_adder full_adder_2 (.Vi(full_adder_1_vi_1), .A(in_7), .B(in_15), .S(out_18), .Vi_1(full_adder_2_vi_1));
  full_adder full_adder_3 (.Vi(full_adder_2_vi_1), .A(in_6), .B(in_14), .S(out_19), .Vi_1(full_adder_3_vi_1));
  full_adder full_adder_4 (.Vi(full_adder_3_vi_1), .A(in_5), .B(in_13), .S(out_20), .Vi_1(full_adder_4_vi_1));
  full_adder full_adder_5 (.Vi(full_adder_4_vi_1), .A(in_4), .B(in_12), .S(out_21), .Vi_1(full_adder_5_vi_1));
  full_adder full_adder_6 (.Vi(full_adder_5_vi_1), .A(in_3), .B(in_11), .S(out_22), .Vi_1(full_adder_6_vi_1));
  full_adder full_adder_7 (.Vi(full_adder_6_vi_1), .A(in_2), .B(in_10), .S(out_23), .Vi_1(full_adder_7_vi_1));
  full_adder full_adder_8 (.Vi(full_adder_7_vi_1), .A(A7), .B(B7), .S(R7), .Vi_1(full_adder_8_vi_1));
  // Probe on full_adder_8_vi_1
endmodule

// 8 Bits Mult
module _8bit_multiplier (
  input  A3,
  input  in_2,
  input  in_3,
  input  A0,
  input  B3,
  input  in_6,
  input  in_7,
  input  B0,
  output R0,
  output out_10,
  output out_11,
  output out_12,
  output out_13,
  output out_14,
  output out_15,
  output R7
);

  wire and_1_out, and_2_out, and_3_out, and_4_out, and_5_out, and_6_out, and_7_out, and_8_out,
       n8bit_adder_1_out_18, n8bit_adder_1_out_19, n8bit_adder_1_out_20, n8bit_adder_1_out_21,
       n8bit_adder_1_out_22, n8bit_adder_1_out_23, n8bit_adder_1_r0, n8bit_adder_1_r7, n8bit_adder_2_out_18,
       n8bit_adder_2_out_19, n8bit_adder_2_out_20, n8bit_adder_2_out_21, n8bit_adder_2_out_22,
       n8bit_adder_2_out_23, n8bit_adder_2_r0, n8bit_adder_2_r7, P0_out, P3_out, P4_out, P7_out, P8_out,
       P11_out, P12_out, P15_out;

  and P0 (P0_out, B0, A0);
  and and_1 (and_1_out, B0, in_3);
  and and_2 (and_2_out, B0, in_2);
  and P3 (P3_out, B0, A3);
  and P4 (P4_out, in_7, A0);
  and and_3 (and_3_out, in_7, in_3);
  and and_4 (and_4_out, in_7, in_2);
  and P7 (P7_out, in_7, A3);
  and P8 (P8_out, in_6, A0);
  and and_5 (and_5_out, in_6, in_3);
  and and_6 (and_6_out, in_6, in_2);
  and P11 (P11_out, in_6, A3);
  and P12 (P12_out, B3, A0);
  and and_7 (and_7_out, B3, in_3);
  and and_8 (and_8_out, B3, in_2);
  and P15 (P15_out, B3, A3);
  _8bit_adder u_8bit_adder_1 (
    .R0(n8bit_adder_1_r0), .out_18(n8bit_adder_1_out_18), .out_19(n8bit_adder_1_out_19),
    .out_20(n8bit_adder_1_out_20), .out_21(n8bit_adder_1_out_21), .out_22(n8bit_adder_1_out_22),
    .out_23(n8bit_adder_1_out_23), .R7(n8bit_adder_1_r7), .A7(1'b0), .in_2(1'b0), .in_3(1'b0), .in_4(P7_out),
    .in_5(and_4_out), .in_6(and_3_out), .in_7(P4_out), .A0(1'b0), .B7(1'b0), .in_10(1'b0), .in_11(1'b0),
    .in_12(1'b0), .in_13(P3_out), .in_14(and_2_out), .in_15(and_1_out), .B0(P0_out));
  _8bit_adder u_8bit_adder_2 (
    .R0(n8bit_adder_2_r0), .out_18(n8bit_adder_2_out_18), .out_19(n8bit_adder_2_out_19),
    .out_20(n8bit_adder_2_out_20), .out_21(n8bit_adder_2_out_21), .out_22(n8bit_adder_2_out_22),
    .out_23(n8bit_adder_2_out_23), .R7(n8bit_adder_2_r7), .A7(1'b0), .in_2(1'b0), .in_3(P11_out),
    .in_4(and_6_out), .in_5(and_5_out), .in_6(P8_out), .in_7(1'b0), .A0(1'b0), .B7(n8bit_adder_1_r7),
    .in_10(n8bit_adder_1_out_23), .in_11(n8bit_adder_1_out_22), .in_12(n8bit_adder_1_out_21),
    .in_13(n8bit_adder_1_out_20), .in_14(n8bit_adder_1_out_19), .in_15(n8bit_adder_1_out_18),
    .B0(n8bit_adder_1_r0));
  _8bit_adder u_8bit_adder_3 (
    .R0(R0), .out_18(out_10), .out_19(out_11), .out_20(out_12), .out_21(out_13), .out_22(out_14),
    .out_23(out_15), .R7(R7), .A7(1'b0), .in_2(P15_out), .in_3(and_8_out), .in_4(and_7_out), .in_5(P12_out),
    .in_6(1'b0), .in_7(1'b0), .A0(1'b0), .B7(n8bit_adder_2_r7), .in_10(n8bit_adder_2_out_23),
    .in_11(n8bit_adder_2_out_22), .in_12(n8bit_adder_2_out_21), .in_13(n8bit_adder_2_out_20),
    .in_14(n8bit_adder_2_out_19), .in_15(n8bit_adder_2_out_18), .B0(n8bit_adder_2_r0));
endmodule

module hex_transcoder (
  input  I0,
  input  in_2,
  input  in_3,
  input  I4,
  output out_5,
  output out_6,
  output out_7,
  output out_8,
  output out_9,
  output out_10,
  output out_11
);

  L0 l0_1 (.D(I0), .in_2(in_2), .in_3(in_3), .A(I4), .out_5(out_5));
  L1 l1_1 (.D(I0), .in_2(in_2), .in_3(in_3), .A(I4), .out_5(out_6));
  L2 l2_1 (.D(I0), .in_2(in_2), .in_3(in_3), .A(I4), .out_5(out_7));
  L3 l3_1 (.D(I0), .in_2(in_2), .in_3(in_3), .A(I4), .out_5(out_8));
  L4 l4_1 (.in_1(I0), .in_2(in_2), .in_3(in_3), .in_4(I4), .out_5(out_9));
  L5 l5_1 (.in_1(I0), .in_2(in_2), .in_3(in_3), .in_4(I4), .out_5(out_10));
  L6 l6_1 (.in_1(I0), .in_2(in_2), .in_3(in_3), .in_4(I4), .out_5(out_11));
endmodule

module L0 (
  input  D,
  input  in_2,
  input  in_3,
  input  A,
  output out_5
);

  wire and_1_out, and_2_out, and_3_out, and_4_out, and_5_out;

  and and_1 (and_1_out, ~A, in_3);  // AND_Gate
  and and_2 (and_2_out, A, ~in_3);  // AND_Gate
  and and_3 (and_3_out, ~in_2, D);  // AND_Gate
  and and_4 (and_4_out, ~A, ~in_2);  // AND_Gate
  and and_5 (and_5_out, ~A, D);  // AND_Gate
  or or_1 (out_5, and_1_out, and_2_out, and_3_out, and_4_out, and_5_out);
endmodule

module L1 (
  input  D,
  input  in_2,
  input  in_3,
  input  A,
  output out_5
);

  wire and_1_out, and_2_out, and_3_out, and_4_out, and_5_out, and_6_out;

  and and_1 (and_1_out, A, in_3, ~in_2);  // AND_Gate
  and and_2 (and_2_out, in_3, ~in_2, D);  // AND_Gate
  and and_3 (and_3_out, ~in_3, ~in_2, ~D);  // AND_Gate
  and and_4 (and_4_out, ~in_3, in_2, D);  // AND_Gate
  and and_5 (and_5_out, ~A, in_2, ~D);  // AND_Gate
  and and_6 (and_6_out, in_3, in_2, ~D);  // AND_Gate
  or or_1 (out_5, and_1_out, and_2_out, and_3_out, and_4_out, and_5_out, and_6_out);
endmodule

module L2 (
  input  D,
  input  in_2,
  input  in_3,
  input  A,
  output out_5
);

  wire and_1_out, and_2_out, and_3_out, and_4_out, and_5_out;

  and and_1 (and_1_out, A, in_3);
  and and_2 (and_2_out, in_2, ~D);  // AND_Gate
  and and_3 (and_3_out, A, in_2);
  and and_4 (and_4_out, A, ~D);  // AND_Gate
  and and_5 (and_5_out, ~A, ~in_3, ~D);  // AND_Gate
  or or_1 (out_5, and_1_out, and_2_out, and_3_out, and_4_out, and_5_out);
endmodule

module L3 (
  input  D,
  input  in_2,
  input  in_3,
  input  A,
  output out_5
);

  wire and_1_out, and_2_out, and_3_out, and_4_out, and_5_out;

  and and_1 (and_1_out, A, ~in_3);  // AND_Gate
  and and_2 (and_2_out, in_2, ~D);  // AND_Gate
  and and_3 (and_3_out, ~A, in_3, ~in_2);  // AND_Gate
  and and_4 (and_4_out, ~in_3, in_2);  // AND_Gate
  and and_5 (and_5_out, A, D);
  or or_1 (out_5, and_1_out, and_2_out, and_3_out, and_4_out, and_5_out);
endmodule

module L4 (
  input  in_1,
  input  in_2,
  input  in_3,
  input  in_4,
  output out_5
);

  wire and_1_out, and_2_out, and_3_out, and_4_out, and_5_out;

  and and_1 (and_1_out, in_4, ~in_3);  // AND_Gate
  and and_2 (and_2_out, ~in_2, ~in_1);  // AND_Gate
  and and_3 (and_3_out, in_4, in_2);
  and and_4 (and_4_out, in_3, ~in_1);  // AND_Gate
  and and_5 (and_5_out, ~in_4, in_3, ~in_2);  // AND_Gate
  or or_1 (out_5, and_1_out, and_2_out, and_3_out, and_4_out, and_5_out);
endmodule

module L5 (
  input  in_1,
  input  in_2,
  input  in_3,
  input  in_4,
  output out_5
);

  wire and_1_out, and_2_out, and_3_out, and_4_out, and_5_out, and_6_out;

  and and_1 (and_1_out, ~in_3, ~in_1);  // AND_Gate
  and and_2 (and_2_out, in_3, in_2);
  and and_3 (and_3_out, ~in_4, in_3, in_1);  // AND_Gate
  and and_4 (and_4_out, ~in_4, in_2, in_1);  // AND_Gate
  and and_5 (and_5_out, in_4, ~in_2, ~in_1);  // AND_Gate
  and and_6 (and_6_out, ~in_4, in_3, ~in_2);  // AND_Gate
  or or_1 (out_5, and_1_out, and_2_out, and_3_out, and_4_out, and_5_out, and_6_out);
endmodule

module L6 (
  input  in_1,
  input  in_2,
  input  in_3,
  input  in_4,
  output out_5
);

  wire and_1_out, and_2_out, and_3_out, and_4_out, and_5_out;

  and and_1 (and_1_out, ~in_4, ~in_3);  // AND_Gate
  and and_2 (and_2_out, ~in_3, ~in_2);  // AND_Gate
  and and_3 (and_3_out, in_4, ~in_2, in_1);  // AND_Gate
  and and_4 (and_4_out, ~in_4, in_2, in_1);  // AND_Gate
  and and_5 (and_5_out, ~in_4, ~in_2, ~in_1);  // AND_Gate
  or or_1 (out_5, and_1_out, and_2_out, and_3_out, and_4_out, and_5_out);
endmodule
