// Logisim project 7led_display.circ as structural Verilog: 12 circuits, main circuit main
module main (
  input  [3:0] A,
  input  [3:0] B
);

  wire input_handler_1_l0, input_handler_1_l1, input_handler_1_l2, input_handler_1_l3, input_handler_1_l4,
       input_handler_1_l5, input_handler_1_l6, input_handler_1_n, n4_bit_subtractor_1_p,
       n4_bit_subtractor_1_s0, n4_bit_subtractor_1_s1, n4_bit_subtractor_1_s2, n4_bit_subtractor_1_s3;

  _4_bit_subtractor u_4_bit_subtractor_1 (
    .S0(n4_bit_subtractor_1_s0), .S1(n4_bit_subtractor_1_s1), .S2(n4_bit_subtractor_1_s2),
    .S3(n4_bit_subtractor_1_s3), .A3(A[3]), .A2(A[2]), .A1(A[1]), .A0(A[0]), .B3(B[3]), .B2(B[2]), .B1(B[1]),
    .B0(B[0]), .P(n4_bit_subtractor_1_p));
  input_handler input_handler_1 (
    .D(n4_bit_subtractor_1_s0), .C(n4_bit_subtractor_1_s1), .B(n4_bit_subtractor_1_s2),
    .A(n4_bit_subtractor_1_s3), .L0(input_handler_1_l0), .L1(input_handler_1_l1), .L2(input_handler_1_l2),
    .L3(input_handler_1_l3), .L4(input_handler_1_l4), .L5(input_handler_1_l5), .L6(input_handler_1_l6),
    .P(n4_bit_subtractor_1_p), .N(input_handler_1_n));
  _7_Segment_Display u_7_segment_display_1 (
    .g(input_handler_1_l3), .f(input_handler_1_l4), .a(input_handler_1_l5), .b(input_handler_1_l6),
    .e(input_handler_1_l2), .d(input_handler_1_l1), .c(input_handler_1_l0), .dp(input_handler_1_n));
endmodule

// FA
module full_adder (
  input  Vi,
  input  Ai,
  input  Bi,
  output Si,
  output Si_1
);

  wire AB_out, AVi_out, BVi_out;

  and AB (AB_out, Vi, Ai);
  and BVi (BVi_out, Vi, Bi);
  and AVi (AVi_out, Ai, Bi);
  xor xor_1 (Si, Vi, Ai, Bi);
  or or_1 (Si_1, AB_out, BVi_out, AVi_out);
endmodule

// SUB
module _4_bit_subtractor (
  input  A3,
  input  A2,
  input  A1,
  input  A0,
  input  B3,
  input  B2,
  input  B1,
  input  B0,
  output S0,
  output S1,
  output S2,
  output S3,
  output P
);

  wire full_adder_1_si_1, full_adder_2_si_1, full_adder_3_si_1, not_1_out, not_2_out, not_3_out, not_4_out;

  not not_1 (not_1_out, B3);
  not not_2 (not_2_out, B2);
  not not_3 (not_3_out, B0);
  not not_4 (not_4_out, B1);
  full_adder full_adder_1 (.Vi(1'b1), .Ai(A0), .Bi(not_3_out), .Si(S0), .Si_1(full_adder_1_si_1));
  full_adder full_adder_2 (.Vi(full_adder_1_si_1), .Ai(A1), .Bi(not_4_out), .Si(S1), .Si_1(full_adder_2_si_1));
  full_adder full_adder_3 (.Vi(full_adder_2_si_1), .Ai(A2), .Bi(not_2_out), .Si(S2), .Si_1(full_adder_3_si_1));
  full_adder full_adder_4 (.Vi(full_adder_3_si_1), .Ai(A3), .Bi(not_1_out), .Si(S3), .Si_1(P));
endmodule

// BCD Converter
module input_handler (
  input  D,
  input  C,
  input  B,
  input  A,
  input  P,
  output L0,
  output L1,
  output L2,
  output L3,
  output L4,
  output L5,
  output L6,
  output N
);

  wire full_adder_1_si_1, full_adder_2_si_1, full_adder_3_si_1, full_adder_4_si_1, not_2_out, not_3_out,
       not_4_out, not_5_out;
  wire [3:0] full_adder_1_si, n4bits_mux_2_1_1_out_4;

  not not_1 (N, P);
  not not_2 (not_2_out, D);
  not not_3 (not_3_out, C);
  not not_4 (not_4_out, B);
  not not_5 (not_5_out, A);
  full_adder full_adder_1 (.Vi(1'b1), .Ai(not_2_out), .Bi(1'b0), .Si(full_adder_1_si[0]), .Si_1(full_adder_1_si_1));
  full_adder full_adder_2 (
    .Vi(full_adder_1_si_1), .Ai(not_3_out), .Bi(1'b0), .Si(full_adder_1_si[1]), .Si_1(full_adder_2_si_1));
  full_adder full_adder_3 (
    .Vi(full_adder_2_si_1), .Ai(not_4_out), .Bi(1'b0), .Si(full_adder_1_si[2]), .Si_1(full_adder_3_si_1));
  full_adder full_adder_4 (
    .Vi(full_adder_3_si_1), .Ai(not_5_out), .Bi(1'b0), .Si(full_adder_1_si[3]), .Si_1(full_adder_4_si_1));
  // Probe on full_adder_4_si_1
  _4bits_mux_2_1 u_4bits_mux_2_1_1 (.A({A, B, C, D}), .B(full_adder_1_si), .out_4(n4bits_mux_2_1_1_out_4), .S(N));
  led_0 led_0_1 (
    .D(n4bits_mux_2_1_1_out_4[0]), .C(n4bits_mux_2_1_1_out_4[1]), .B(n4bits_mux_2_1_1_out_4[2]),
    .A(n4bits_mux_2_1_1_out_4[3]), .L0(L0));
  led_1 led_1_1 (
    .D(n4bits_mux_2_1_1_out_4[0]), .C(n4bits_mux_2_1_1_out_4[1]), .B(n4bits_mux_2_1_1_out_4[2]),
    .A(n4bits_mux_2_1_1_out_4[3]), .L1(L1));
  led_2 led_2_1 (
    .in_1(n4bits_mux_2_1_1_out_4[0]), .in_2(n4bits_mux_2_1_1_out_4[1]), .in_3(n4bits_mux_2_1_1_out_4[2]),
    .in_4(n4bits_mux_2_1_1_out_4[3]), .out_5(L2));
  led_3 led_3_1 (
    .D(n4bits_mux_2_1_1_out_4[0]), .C(n4bits_mux_2_1_1_out_4[1]), .B(n4bits_mux_2_1_1_out_4[2]),
    .A(n4bits_mux_2_1_1_out_4[3]), .L3(L3));
  led_4 led_4_1 (
    .D(n4bits_mux_2_1_1_out_4[0]), .C(n4bits_mux_2_1_1_out_4[1]), .B(n4bits_mux_2_1_1_out_4[2]),
    .A(n4bits_mux_2_1_1_out_4[3]), .L4(L4));
  led_5 led_5_1 (
    .D(n4bits_mux_2_1_1_out_4[0]), .C(n4bits_mux_2_1_1_out_4[1]), .B(n4bits_mux_2_1_1_out_4[2]),
    .A(n4bits_mux_2_1_1_out_4[3]), .L5(L5));
  led_6 led_6_1 (
    .D(n4bits_mux_2_1_1_out_4[0]), .C(n4bits_mux_2_1_1_out_4[1]), .B(n4bits_mux_2_1_1_out_4[2]),
    .A(n4bits_mux_2_1_1_out_4[3]), .L6(L6));
endmodule

// L0
module led_0 (
  input  D,
  input  C,
  input  B,
  input  A,
  output L0
);

  wire A_prime_B_out, A_prime_D_out, C_prime_B_prime_out;

  and A_prime_D (A_prime_D_out, ~A, D);  // AND_Gate
  and A_prime_B (A_prime_B_out, ~A, B);  // AND_Gate
  and C_prime_B_prime (C_prime_B_prime_out, ~B, ~C);  // AND_Gate
  or or_1 (L0, A_prime_D_out, A_prime_B_out, C_prime_B_prime_out);
endmodule

// L6
module led_6 (
  input  D,
  input  C,
  input  B,
  input  A,
  output L6
);

  wire A_prime_B_prime_out, A_prime_C_prime_D_prime_out, A_prime_CD_out, B_prime_C_prime_out;

  and A_prime_B_prime (A_prime_B_prime_out, ~A, ~B);  // AND_Gate
  and B_prime_C_prime (B_prime_C_prime_out, ~B, ~C);  // AND_Gate
  and A_prime_C_prime_D_prime (A_prime_C_prime_D_prime_out, ~A, ~C, ~D);  // AND_Gate
  and A_prime_CD (A_prime_CD_out, ~A, C, D);  // AND_Gate
  or or_1 (L6, A_prime_B_prime_out, B_prime_C_prime_out, A_prime_C_prime_D_prime_out, A_prime_CD_out);
endmodule

// L2
module led_2 (
  input  in_1,
  input  in_2,
  input  in_3,
  input  in_4,
  output out_5
);

  wire A_C_prime_D_prime_out, B_prime_C_prime_D_prime_out;

  and B_prime_C_prime_D_prime (B_prime_C_prime_D_prime_out, ~in_3, ~in_2, ~in_1);  // AND_Gate
  and A_C_prime_D_prime (A_C_prime_D_prime_out, ~in_4, in_2, ~in_1);  // AND_Gate
  or or_1 (out_5, B_prime_C_prime_D_prime_out, A_C_prime_D_prime_out);
endmodule

// L4
module led_4 (
  input  D,
  input  C,
  input  B,
  input  A,
  output L4
);

  wire A_prime_BC_prime_out, A_prime_BD_prime_out, A_prime_C_prime_D_prime_out, AB_prime_C_prime_out;

  and A_prime_C_prime_D_prime (A_prime_C_prime_D_prime_out, ~A, ~C, ~D);  // AND_Gate
  and A_prime_BD_prime (A_prime_BD_prime_out, ~A, B, ~D);  // AND_Gate
  and AB_prime_C_prime (AB_prime_C_prime_out, A, ~B, ~C);  // AND_Gate
  and A_prime_BC_prime (A_prime_BC_prime_out, ~A, B, ~C);  // AND_Gate
  or or_1 (L4, A_prime_C_prime_D_prime_out, A_prime_BD_prime_out, AB_prime_C_prime_out, A_prime_BC_prime_out);
endmodule

// L5
module led_5 (
  input  D,
  input  C,
  input  B,
  input  A,
  output L5
);

  wire A_prime_B_prime_D_prime_out, A_prime_BD_out, A_prime_C_out, AB_prime_C_prime_out;

  and A_prime_C (A_prime_C_out, ~A, C);  // AND_Gate
  and A_prime_B_prime_D_prime (A_prime_B_prime_D_prime_out, ~A, ~B, ~D);  // AND_Gate
  and AB_prime_C_prime (AB_prime_C_prime_out, A, ~B, ~C);  // AND_Gate
  and A_prime_BD (A_prime_BD_out, ~A, B, D);  // AND_Gate
  or or_1 (L5, A_prime_C_out, A_prime_B_prime_D_prime_out, AB_prime_C_prime_out, A_prime_BD_out);
endmodule

// L1
module led_1 (
  input  D,
  input  C,
  input  B,
  input  A,
  output L1
);

  wire A_prime_B_prime_C_out, A_prime_BC_prime_D_out, A_prime_CD_prime_out, B_prime_C_prime_D_prime_out;

  and B_prime_C_prime_D_prime (B_prime_C_prime_D_prime_out, ~B, ~C, ~D);  // AND_Gate
  and A_prime_B_prime_C (A_prime_B_prime_C_out, ~A, ~B, C);  // AND_Gate
  and A_prime_CD_prime (A_prime_CD_prime_out, ~A, C, ~D);  // AND_Gate
  and A_prime_BC_prime_D (A_prime_BC_prime_D_out, ~A, B, ~C, D);  // AND_Gate
  or or_1 (L1, B_prime_C_prime_D_prime_out, A_prime_B_prime_C_out, A_prime_CD_prime_out, A_prime_BC_prime_D_out);
endmodule

// L3
module led_3 (
  input  D,
  input  C,
  input  B,
  input  A,
  output L3
);

  wire B_prime_C_out, BC_prime_out, CD_prime_out;

  and CD_prime (CD_prime_out, C, ~D);  // AND_Gate
  and B_prime_C (B_prime_C_out, ~B, C);  // AND_Gate
  and BC_prime (BC_prime_out, B, ~C);  // AND_Gate
  or or_1 (L3, A, CD_prime_out, B_prime_C_out, BC_prime_out);
endmodule

// MUX
module _4bits_mux_2_1 (
  input  [3:0] A,
  input  [3:0] B,
  input  S,
  output [3:0] out_4
);

  wire and_1_out, and_2_out, and_3_out, and_4_out, and_5_out, and_6_out, and_7_out, and_8_out;

  and and_1 (and_1_out, A[0], ~S);  // AND_Gate
  and and_2 (and_2_out, A[1], ~S);  // AND_Gate
  and and_3 (and_3_out, A[2], ~S);  // AND_Gate
  and and_4 (and_4_out, A[3], ~S);  // AND_Gate
  and and_5 (and_5_out, B[0], S);
  and and_6 (and_6_out, B[1], S);
  and and_7 (and_7_out, B[2], S);
  and and_8 (and_8_out, B[3], S);
  or or_1 (out_4[0], and_1_out, and_5_out);
  or or_2 (out_4[1], and_2_out, and_6_out);
  or or_3 (out_4[2], and_3_out, and_7_out);
  or or_4 (out_4[3], and_4_out, and_8_out);
endmodule
