// Logisim project setacarro.circ as structural Verilog: 13 circuits, main circuit main
module main (
  input  in_1,
  input  in_2,
  input  in_3
);

  wire button_1_out, clock_1_out, d1_1_out_2, d2_1_out_2, d3_1_out_2, e1_1_out_2, e2_1_out_2, e3_1_out_2,
       p1_1_out_3, p2_1_out_3, p3_1_out_3;
  wire [1:0] priority_encoder_1_out_4;
  wire [2:0] flip_flop_d_1_out_4;

  Button button_1 (.out(button_1_out));
  Clock clock_1 (.out(clock_1_out));
  flip_flop_d flip_flop_d_1 (
    .in_1(p1_1_out_3), .out_4(flip_flop_d_1_out_4[0]), .in_2(clock_1_out), .in_3(button_1_out));
  flip_flop_d flip_flop_d_2 (
    .in_1(p2_1_out_3), .out_4(flip_flop_d_1_out_4[1]), .in_2(clock_1_out), .in_3(button_1_out));
  flip_flop_d flip_flop_d_3 (
    .in_1(p3_1_out_3), .out_4(flip_flop_d_1_out_4[2]), .in_2(clock_1_out), .in_3(button_1_out));
  // Probe on priority_encoder_1_out_4
  priority_encoder priority_encoder_1 (.in_1(in_1), .in_2(in_2), .in_3(in_3), .out_4(priority_encoder_1_out_4));
  // Probe on flip_flop_d_1_out_4
  E2 e2_1 (.in_1(flip_flop_d_1_out_4), .out_2(e2_1_out_2));
  E3 e3_1 (.in_1(flip_flop_d_1_out_4), .out_2(e3_1_out_2));
  LED led_1 (.in(e2_1_out_2));
  LED led_2 (.in(e3_1_out_2));
  D1 d1_1 (.in_1(flip_flop_d_1_out_4), .out_2(d1_1_out_2));
  E1 e1_1 (.in_1(flip_flop_d_1_out_4), .out_2(e1_1_out_2));
  LED led_3 (.in(d1_1_out_2));
  LED led_4 (.in(e1_1_out_2));
  D3 d3_1 (.in_1(flip_flop_d_1_out_4), .out_2(d3_1_out_2));
  D2 d2_1 (.in_1(flip_flop_d_1_out_4), .out_2(d2_1_out_2));
  LED led_5 (.in(d3_1_out_2));
  LED led_6 (.in(d2_1_out_2));
  P1 p1_1 (.in_1(flip_flop_d_1_out_4), .in_2(priority_encoder_1_out_4), .out_3(p1_1_out_3));
  P2 p2_1 (.in_1(flip_flop_d_1_out_4), .in_2(priority_encoder_1_out_4), .out_3(p2_1_out_3));
  P3 p3_1 (.in_1(flip_flop_d_1_out_4), .in_2(priority_encoder_1_out_4), .out_3(p3_1_out_3));
endmodule

module latch_d (
  input  in_1,
  input  in_2,
  output out_3,
  output out_4
);

  wire and_1_out, and_2_out, not_1_out;

  and and_1 (and_1_out, in_1, in_2);
  and and_2 (and_2_out, in_2, not_1_out);
  not not_1 (not_1_out, in_1);
  nor nor_1 (out_3, and_1_out, out_4);
  nor nor_2 (out_4, out_3, and_2_out);
endmodule

module flip_flop_d (
  input  in_1,
  input  in_2,
  input  in_3,
  output out_4
);

  wire latch_d_1_out_3, latch_d_1_out_4, latch_d_2_out_3, latch_d_2_out_4, not_1_out;

  latch_d latch_d_1 (.in_1(in_1), .in_2(in_2), .out_3(latch_d_1_out_3), .out_4(latch_d_1_out_4));
  not not_1 (not_1_out, in_2);
  // Probe on latch_d_1_out_4
  latch_d latch_d_2 (.in_1(latch_d_1_out_3), .in_2(not_1_out), .out_3(latch_d_2_out_3), .out_4(latch_d_2_out_4));
  // Probe on latch_d_2_out_4
  and and_1 (out_4, latch_d_2_out_3, ~in_3);  // AND_Gate
endmodule

module priority_encoder (
  input  in_1,
  input  in_2,
  input  in_3,
  output [1:0] out_4
);

  wire and_1_out;

  and and_1 (and_1_out, in_1, ~in_3);  // AND_Gate
  or or_1 (out_4[0], in_2, in_3);
  or or_2 (out_4[1], in_2, and_1_out);
endmodule

module P1 (
  input  [2:0] in_1,
  input  [1:0] in_2,
  output out_3
);

  wire and_1_out, and_2_out, and_3_out, and_4_out, and_5_out;

  and and_1 (and_1_out, ~in_1[0], in_2[0]);  // AND_Gate
  and and_2 (and_2_out, ~in_1[2], in_2[1], in_2[0]);  // AND_Gate
  and and_3 (and_3_out, in_1[2], ~in_1[1], in_2[0]);  // AND_Gate
  and and_4 (and_4_out, in_1[1], ~in_2[1], in_2[0]);  // AND_Gate
  and and_5 (and_5_out, in_1[2], ~in_1[1], ~in_1[0], in_2[1]);  // AND_Gate
  or or_1 (out_3, and_1_out, and_2_out, and_3_out, and_4_out, and_5_out);
endmodule

module P2 (
  input  [2:0] in_1,
  input  [1:0] in_2,
  output out_3
);

  wire and_1_out, and_2_out, and_3_out, and_4_out, and_5_out;

  and and_1 (and_1_out, ~in_1[2], in_2[1], in_2[0]);  // AND_Gate
  and and_2 (and_2_out, ~in_1[0], in_2[1], in_2[0]);  // AND_Gate
  and and_3 (and_3_out, ~in_1[2], ~in_1[1], in_1[0], in_2[0]);  // AND_Gate
  and and_4 (and_4_out, ~in_1[2], in_1[1], ~in_1[0], in_2[0]);  // AND_Gate
  and and_5 (and_5_out, in_1[2], ~in_1[1], in_1[0], in_2[1]);  // AND_Gate
  or or_1 (out_3, and_1_out, and_2_out, and_3_out, and_4_out, and_5_out);
endmodule

module P3 (
  input  [2:0] in_1,
  input  [1:0] in_2,
  output out_3
);

  wire and_1_out, and_2_out, and_3_out, and_4_out;

  and and_1 (and_1_out, ~in_1[2], in_2[1]);  // AND_Gate
  and and_2 (and_2_out, ~in_1[1], in_2[1]);  // AND_Gate
  and and_3 (and_3_out, ~in_1[0], in_2[1]);  // AND_Gate
  and and_4 (and_4_out, in_2[1], ~in_2[0]);  // AND_Gate
  or or_1 (out_3, and_1_out, and_2_out, and_3_out, and_4_out);
endmodule

module D1 (
  input  [2:0] in_1,
  output out_2
);

  wire and_1_out, and_2_out, and_3_out;

  and and_1 (and_1_out, ~in_1[2], in_1[1]);  // AND_Gate
  and and_2 (and_2_out, ~in_1[2], in_1[0]);  // AND_Gate
  and and_3 (and_3_out, in_1[1], in_1[0]);
  or or_1 (out_2, and_1_out, and_2_out, and_3_out);
endmodule

module D2 (
  input  [2:0] in_1,
  output out_2
);

  wire and_1_out, and_2_out;

  and and_1 (and_1_out, ~in_1[2], in_1[1]);  // AND_Gate
  and and_2 (and_2_out, in_1[1], in_1[0]);
  or or_1 (out_2, and_1_out, and_2_out);
endmodule

module D3 (
  input  [2:0] in_1,
  output out_2
);

  // Probe on in_1[2]
  and and_1 (out_2, in_1[1], in_1[0]);
endmodule

module E1 (
  input  [2:0] in_1,
  output out_2
);

  // Probe on in_1[1]
  // Probe on in_1[0]

  assign out_2 = in_1[2];
endmodule

module E2 (
  input  [2:0] in_1,
  output out_2
);

  wire and_1_out, and_2_out;

  and and_1 (and_1_out, in_1[2], in_1[1]);
  and and_2 (and_2_out, in_1[0], in_1[2]);
  or or_1 (out_2, and_1_out, and_2_out);
endmodule

module E3 (
  input  [2:0] in_1,
  output out_2
);

  // Probe on in_1[0]
  and and_1 (out_2, in_1[2], in_1[1]);
endmodule
