// Logisim project vending_machine.circ as structural Verilog: 16 circuits, main circuit main
// 1 MIN
module main (
);

  wire _50C_out, _100C_out, BA_out, BC_out, BT_out, clock_1_out, d_ff_1_q, d_ff_2_q, d_ff_3_q, d_ff_6_q,
       im_output_1_out_2, la_output_1_out_2, lt_output_1_out_2, n1min_step_counter_1_out_3, p0_1_out_3,
       p1_1_out_3, p2_1_out_3, p3_1_out_3, RESET_out, RESET_WD_out, t50_output_1_out_2, t100_output_1_out_2;
  wire [2:0] priority_encoder_1_out_2;
  wire [3:0] A0_q;
  wire [4:0] and_1_out;

  Button _50C (.out(_50C_out));
  Button _100C (.out(_100C_out));
  Button BA (.out(BA_out));
  Button BT (.out(BT_out));
  Button BC (.out(BC_out));
  Button RESET (.out(RESET_out));
  D_Flip_Flop d_ff_1 (
    .clk(clock_1_out), .D(RESET_out), .Q(d_ff_1_q), .preset(RESET_out), .en(1'b1));  // open: Qn, reset
  or RESET_WD (RESET_WD_out, d_ff_2_q, d_ff_3_q, and_1_out[2], and_1_out[3], d_ff_6_q, d_ff_1_q);
  Clock clock_1 (.out(clock_1_out));
  _1min_step_counter u_1min_step_counter_1 (
    .Reset(RESET_WD_out), .out_3(n1min_step_counter_1_out_3), .Clock(clock_1_out));
  flip_flop_d A0 (.D(p0_1_out_3), .Q(A0_q[0]), .Clk(clock_1_out), .Reset(d_ff_1_q));
  flip_flop_d A1 (.D(p1_1_out_3), .Q(A0_q[1]), .Clk(clock_1_out), .Reset(d_ff_1_q));
  flip_flop_d A2 (.D(p2_1_out_3), .Q(A0_q[2]), .Clk(clock_1_out), .Reset(d_ff_1_q));
  flip_flop_d A3 (.D(p3_1_out_3), .Q(A0_q[3]), .Clk(clock_1_out), .Reset(d_ff_1_q));
  D_Flip_Flop d_ff_2 (.clk(clock_1_out), .D(_50C_out), .Q(d_ff_2_q), .preset(_50C_out), .en(1'b1));  // open: Qn, reset
  D_Flip_Flop d_ff_3 (
    .clk(clock_1_out), .D(_100C_out), .Q(d_ff_3_q), .preset(_100C_out), .en(1'b1));  // open: Qn, reset
  D_Flip_Flop d_ff_4 (.clk(clock_1_out), .D(BA_out), .Q(and_1_out[2]), .preset(BA_out), .en(1'b1));  // open: Qn, reset
  D_Flip_Flop d_ff_5 (.clk(clock_1_out), .D(BT_out), .Q(and_1_out[3]), .preset(BT_out), .en(1'b1));  // open: Qn, reset
  D_Flip_Flop d_ff_6 (.clk(clock_1_out), .D(BC_out), .Q(d_ff_6_q), .preset(BC_out), .en(1'b1));  // open: Qn, reset
  or or_1 (and_1_out[4], d_ff_6_q, n1min_step_counter_1_out_3);
  t50_output t50_output_1 (.in_1(A0_q), .out_2(t50_output_1_out_2));
  t100_output t100_output_1 (.in_1(A0_q), .out_2(t100_output_1_out_2));
  la_output la_output_1 (.in_1(A0_q), .out_2(la_output_1_out_2));
  lt_output lt_output_1 (.in_1(A0_q), .out_2(lt_output_1_out_2));
  im_output im_output_1 (.in_1(A0_q), .out_2(im_output_1_out_2));
  and and_1 (and_1_out[0], d_ff_2_q, ~im_output_1_out_2);  // AND_Gate
  and and_2 (and_1_out[1], ~im_output_1_out_2, d_ff_3_q);  // AND_Gate
  priority_encoder priority_encoder_1 (.in_1(and_1_out), .out_2(priority_encoder_1_out_2));
  P0 p0_1 (.in_1(A0_q), .in_2(priority_encoder_1_out_2), .out_3(p0_1_out_3));
  P1 p1_1 (.out_3(p1_1_out_3), .in_1(A0_q), .in_2(priority_encoder_1_out_2));
  P2 p2_1 (.in_2(priority_encoder_1_out_2), .in_1(A0_q), .out_3(p2_1_out_3));
  P3 p3_1 (.out_3(p3_1_out_3), .in_1(A0_q), .in_2(priority_encoder_1_out_2));
  LED T50 (.in(t50_output_1_out_2));
  LED T100 (.in(t100_output_1_out_2));
  LED LA (.in(la_output_1_out_2));
  LED LT (.in(lt_output_1_out_2));
  LED IM (.in(im_output_1_out_2));
  // Probe on A0_q
endmodule

// SR
module latch_sr (
  input  R,
  input  S,
  output Q,
  output Q_prime
);

  nor nor_1 (Q, R, Q_prime);
  nor nor_2 (Q_prime, Q, S);
endmodule

// En
module enabler (
  input  I1,
  input  E,
  input  I2,
  output O1,
  output O2
);

  and and_1 (O1, I1, E);
  and and_2 (O2, E, I2);
endmodule

// D
module latch_d (
  input  D,
  input  Clk,
  output out_3,
  output out_4
);

  wire enabler_1_o1, enabler_1_o2, not_1_out;

  enabler enabler_1 (.I1(D), .E(Clk), .I2(not_1_out), .O1(enabler_1_o1), .O2(enabler_1_o2));
  not not_1 (not_1_out, D);
  latch_sr latch_sr_1 (.R(enabler_1_o1), .Q(out_3), .Q_prime(out_4), .S(enabler_1_o2));
endmodule

// FF DU
module flip_flop_d (
  input  Clk,
  input  D,
  input  Reset,
  output Q
);

  wire latch_d_1_out_3, latch_d_1_out_4, latch_d_2_out_3, latch_d_2_out_4, not_1_out;

  not not_1 (not_1_out, Clk);
  latch_d latch_d_1 (.D(D), .out_3(latch_d_1_out_3), .out_4(latch_d_1_out_4), .Clk(not_1_out));
  // Probe on latch_d_1_out_4
  latch_d latch_d_2 (.D(latch_d_1_out_3), .out_3(latch_d_2_out_3), .out_4(latch_d_2_out_4), .Clk(Clk));
  // Probe on latch_d_2_out_4
  and and_1 (Q, latch_d_2_out_3, ~Reset);  // AND_Gate
endmodule

// 1 MIN
module _1min_step_counter (
  input  Reset,
  input  Clock,
  output out_3
);

  wire and_1_out, and_2_out, and_3_out, and_4_out, and_5_out, and_6_out, and_7_out, and_8_out,
       flip_flop_d_1_q, flip_flop_d_2_q, flip_flop_d_3_q, flip_flop_d_4_q, flip_flop_d_5_q, flip_flop_d_6_q,
       flip_flop_d_7_q, flip_flop_d_8_q, flip_flop_d_9_q, xor_1_out, xor_2_out, xor_3_out, xor_4_out,
       xor_5_out, xor_6_out, xor_7_out, xor_8_out, xor_9_out;

  and and_1 (and_1_out, 1'b1, flip_flop_d_1_q);
  and and_2 (and_2_out, and_1_out, flip_flop_d_2_q);
  and and_3 (and_3_out, and_2_out, flip_flop_d_3_q);
  and and_4 (and_4_out, and_3_out, flip_flop_d_4_q);
  and and_5 (and_5_out, and_4_out, flip_flop_d_5_q);
  and and_6 (and_6_out, and_5_out, flip_flop_d_6_q);
  and and_7 (and_7_out, and_6_out, flip_flop_d_7_q);
  and and_8 (and_8_out, and_7_out, flip_flop_d_8_q);
  xor xor_1 (xor_1_out, 1'b1, flip_flop_d_1_q);
  xor xor_2 (xor_2_out, and_1_out, flip_flop_d_2_q);
  xor xor_3 (xor_3_out, and_2_out, flip_flop_d_3_q);
  xor xor_4 (xor_4_out, and_3_out, flip_flop_d_4_q);
  xor xor_5 (xor_5_out, and_4_out, flip_flop_d_5_q);
  xor xor_6 (xor_6_out, and_5_out, flip_flop_d_6_q);
  xor xor_7 (xor_7_out, and_6_out, flip_flop_d_7_q);
  xor xor_8 (xor_8_out, and_7_out, flip_flop_d_8_q);
  xor xor_9 (xor_9_out, and_8_out, flip_flop_d_9_q);
  flip_flop_d flip_flop_d_1 (.D(xor_1_out), .Q(flip_flop_d_1_q), .Clk(Clock), .Reset(Reset));
  flip_flop_d flip_flop_d_2 (.D(xor_2_out), .Q(flip_flop_d_2_q), .Clk(Clock), .Reset(Reset));
  flip_flop_d flip_flop_d_3 (.D(xor_3_out), .Q(flip_flop_d_3_q), .Clk(Clock), .Reset(Reset));
  flip_flop_d flip_flop_d_4 (.D(xor_4_out), .Q(flip_flop_d_4_q), .Clk(Clock), .Reset(Reset));
  flip_flop_d flip_flop_d_5 (.D(xor_5_out), .Q(flip_flop_d_5_q), .Clk(Clock), .Reset(Reset));
  flip_flop_d flip_flop_d_6 (.D(xor_6_out), .Q(flip_flop_d_6_q), .Clk(Clock), .Reset(Reset));
  flip_flop_d flip_flop_d_7 (.D(xor_7_out), .Q(flip_flop_d_7_q), .Clk(Clock), .Reset(Reset));
  flip_flop_d flip_flop_d_8 (.D(xor_8_out), .Q(flip_flop_d_8_q), .Clk(Clock), .Reset(Reset));
  flip_flop_d flip_flop_d_9 (.D(xor_9_out), .Q(flip_flop_d_9_q), .Clk(Clock), .Reset(Reset));
  and _480___1_prime (out_3, ~flip_flop_d_1_q, ~flip_flop_d_2_q, ~flip_flop_d_3_q, ~flip_flop_d_4_q, ~flip_flop_d_5_q, flip_flop_d_6_q, flip_flop_d_7_q, flip_flop_d_8_q, flip_flop_d_9_q);  // AND_Gate
endmodule

// T50
module t50_output (
  input  [3:0] in_1,
  output out_2
);

  and A3A2_prime_A1_prime_A0 (out_2, ~in_1[0], in_1[1], ~in_1[2], in_1[3]);  // AND_Gate
endmodule

// T100
module t100_output (
  input  [3:0] in_1,
  output out_2
);

  wire A3A1A0_out, A3A2_out;

  and A3A2 (A3A2_out, in_1[2], in_1[3]);
  and A3A1A0 (A3A1A0_out, in_1[0], in_1[1], in_1[3]);
  or or_1 (out_2, A3A2_out, A3A1A0_out);
endmodule

// LA
module la_output (
  input  [3:0] in_1,
  output out_2
);

  wire A2A1_out, A3_prime_A2A0_out;

  and A3_prime_A2A0 (A3_prime_A2A0_out, in_1[0], in_1[2], ~in_1[3]);  // AND_Gate
  and A2A1 (A2A1_out, in_1[1], in_1[2]);
  or or_1 (out_2, A3_prime_A2A0_out, A2A1_out);
endmodule

// LT
module lt_output (
  input  [3:0] in_1,
  output out_2
);

  // Probe on in_1[0]
  and A3A2_prime_A1_prime (out_2, ~in_1[1], ~in_1[2], in_1[3]);  // AND_Gate
endmodule

// IM
module im_output (
  input  [3:0] in_1,
  output out_2
);

  wire A1A0_out, A3A2_prime_out;

  and A1A0 (A1A0_out, in_1[0], in_1[1]);
  and A3A2_prime (A3A2_prime_out, ~in_1[2], in_1[3]);  // AND_Gate
  or or_1 (out_2, in_1[2], A1A0_out, A3A2_prime_out);
endmodule

// PE
module priority_encoder (
  input  [4:0] in_1,
  output [2:0] out_2
);

  wire and_1_out, and_2_out, and_3_out, and_4_out, and_5_out, and_6_out;

  and and_1 (and_1_out, ~in_1[1], in_1[2]);  // AND_Gate
  and and_2 (and_2_out, ~in_1[1], ~in_1[3], in_1[4]);  // AND_Gate
  and and_3 (and_3_out, ~in_1[0], ~in_1[1], in_1[2]);  // AND_Gate
  and and_4 (and_4_out, ~in_1[0], in_1[1], ~in_1[2]);  // AND_Gate
  and and_5 (and_5_out, ~in_1[0], ~in_1[1], ~in_1[2], in_1[3]);  // AND_Gate
  and and_6 (and_6_out, ~in_1[0], ~in_1[1], ~in_1[2], in_1[4]);  // AND_Gate
  or or_1 (out_2[0], in_1[0], and_1_out, and_2_out);
  or or_2 (out_2[1], and_3_out, and_4_out);
  or or_3 (out_2[2], and_5_out, and_6_out);
endmodule

module P0 (
  input  [3:0] in_1,
  input  [2:0] in_2,
  output out_3
);

  wire and_1_out, and_2_out, and_3_out, and_4_out, and_5_out, and_6_out, and_7_out, and_8_out, and_9_out,
       and_10_out;

  and and_1 (and_1_out, in_1[2], in_1[1], in_1[0]);
  and and_2 (and_2_out, in_1[3], in_1[2], in_1[0]);
  and and_3 (and_3_out, ~in_1[3], ~in_1[2], in_1[0], ~in_2[2], ~in_2[0]);  // AND_Gate
  and and_4 (and_4_out, ~in_1[3], in_1[1], in_1[0], ~in_2[2], ~in_2[0]);  // AND_Gate
  and and_5 (and_5_out, ~in_1[3], ~in_1[2], ~in_1[1], in_1[0], ~in_2[0]);  // AND_Gate
  and and_6 (and_6_out, ~in_1[3], ~in_1[2], ~in_1[1], in_1[0], in_2[1]);  // AND_Gate
  and and_7 (and_7_out, ~in_1[3], ~in_1[2], in_1[1], ~in_1[0], in_2[0]);  // AND_Gate
  and and_8 (and_8_out, ~in_1[3], in_1[2], ~in_1[1], ~in_1[0], in_2[2]);  // AND_Gate
  and and_9 (and_9_out, ~in_1[3], ~in_1[2], ~in_1[0], ~in_2[2], ~in_2[1], in_2[0]);  // AND_Gate
  and and_10 (and_10_out, ~in_1[3], in_1[2], ~in_1[1], ~in_1[0], in_2[1], in_2[0]);  // AND_Gate
  or or_1 (out_3, and_1_out, and_2_out, and_3_out, and_4_out, and_5_out, and_6_out, and_7_out, and_8_out, and_9_out, and_10_out);
endmodule

module P1 (
  input  [3:0] in_1,
  input  [2:0] in_2,
  output out_3
);

  wire and_1_out, and_2_out, and_3_out, and_4_out, and_5_out, and_6_out, and_7_out, and_8_out;

  and and_1 (and_1_out, in_1[2], in_1[1]);
  and and_2 (and_2_out, in_1[3], in_1[2]);
  and and_3 (and_3_out, in_1[3], ~in_1[1], in_1[0]);  // AND_Gate
  and and_4 (and_4_out, ~in_1[3], in_1[1], ~in_1[0], ~in_2[1]);  // AND_Gate
  and and_5 (and_5_out, ~in_1[3], in_1[1], in_1[0], ~in_2[2]);  // AND_Gate
  and and_6 (and_6_out, in_1[2], ~in_1[0], in_2[1], in_2[0]);  // AND_Gate
  and and_7 (and_7_out, ~in_1[2], ~in_1[1], in_1[0], ~in_2[1], in_2[0]);  // AND_Gate
  and and_8 (and_8_out, ~in_1[3], ~in_1[2], ~in_1[1], in_2[1], ~in_2[0]);  // AND_Gate
  or or_1 (out_3, and_1_out, and_2_out, and_3_out, and_4_out, and_5_out, and_6_out, and_7_out, and_8_out);
endmodule

module P2 (
  input  [3:0] in_1,
  input  [2:0] in_2,
  output out_3
);

  wire and_1_out, and_2_out, and_3_out, and_4_out, and_5_out;

  and and_1 (and_1_out, ~in_1[3], in_1[2], ~in_1[1], ~in_1[0], ~in_2[2]);  // AND_Gate
  and and_2 (and_2_out, ~in_1[3], ~in_1[2], in_1[1], ~in_1[0], in_2[1]);  // AND_Gate
  and and_3 (and_3_out, ~in_1[3], ~in_1[2], in_1[1], in_2[1], in_2[0]);  // AND_Gate
  and and_4 (and_4_out, ~in_1[3], in_1[2], ~in_1[1], ~in_1[0], in_2[0]);  // AND_Gate
  and and_5 (and_5_out, ~in_1[3], ~in_1[2], in_1[1], in_1[0], in_2[2], in_2[0]);  // AND_Gate
  or or_1 (out_3, and_1_out, and_2_out, and_3_out, and_4_out, and_5_out);
endmodule

module P3 (
  input  [3:0] in_1,
  input  [2:0] in_2,
  output out_3
);

  wire and_1_out, and_2_out, and_3_out, and_4_out, and_5_out, and_6_out, and_7_out;

  // Probe on in_2[1]
  and and_1 (and_1_out, in_1[3], in_1[2]);
  and and_2 (and_2_out, in_1[2], in_1[1]);
  and and_3 (and_3_out, in_1[3], ~in_1[1], in_1[0]);  // AND_Gate
  and and_4 (and_4_out, in_1[2], ~in_1[0], in_2[2]);  // AND_Gate
  and and_5 (and_5_out, ~in_1[3], in_1[1], in_2[2], in_2[0]);  // AND_Gate
  and and_6 (and_6_out, ~in_1[3], in_1[1], in_1[0], in_2[2]);  // AND_Gate
  and and_7 (and_7_out, ~in_1[3], ~in_1[2], in_1[0], in_2[2], in_2[0]);  // AND_Gate
  or or_1 (out_3, and_1_out, and_2_out, and_3_out, and_4_out, and_5_out, and_6_out, and_7_out);
endmodule
